# Fritzing sketch ObjetsCommunicantsFritzing (saved by Fritzing 0.9.3b)
breadboards: 1

parts:
  Composant1 = Arduino Leonardo (Rev3b)
  R1 = Resistor [tolerance=±5% resistance=220 package=THT]
  R2 = Resistor [tolerance=±5% resistance=220 package=THT]
  R3 = Resistor [tolerance=±5% resistance=220 package=THT]
  R4 = Resistor [tolerance=±5% resistance=220 package=THT]
  R5 = Resistor [tolerance=±5% resistance=220 package=THT]
  R6 = Resistor [tolerance=±5% resistance=220 package=THT]
  R7 = Resistor [tolerance=±5% resistance=220 package=THT]
  R8 = Resistor [tolerance=±5% resistance=220 package=THT]
  Disp1 = LBT2088AH [part_number=LBT2088AH]
  Disp2 = LBT2088AH [part_number=LBT2088AH]
  Composant2 = SRF05 Ultrasonic Rangefinder
  Composant3 = SRF05 Ultrasonic Rangefinder

nets:
  N1: Composant1.D0/RX, Composant2.Echo
  N2: Composant1.D1/TX, Composant3.Echo
  N3: Composant1.D2/SDA, Disp1.pin_13, Disp2.pin_13
  N4: Composant1.D3_PWM/SCL, Disp1.pin_10, Disp2.pin_10
  N5: Composant1.D4/A6, Disp1.pin_15, Disp2.pin_15
  N6: Composant1.D5_PWM, Disp1.pin_9, Disp2.pin_9
  N7: Composant1.D6_PWM/A7, R5.Pin_1
  N8: Composant1.D7, Disp1.pin_16, Disp2.pin_16
  VCC: Composant1.5V, Composant2.VCC, Composant3.VCC
  GND: Composant1.GND, Composant2.GND, Composant3.GND
  N9: Composant1.A0, Disp1.pin_14, Disp2.pin_14
  N10: Composant1.A1, R6.Pin_1
  N11: Composant1.A2, R2.Pin_1
  N12: Composant1.A3, R1.Pin_1
  N13: Composant1.A4, Disp1.pin_12, Disp2.pin_12
  N14: Composant1.D8/A8, R3.Pin_1
  N15: Composant1.D9_PWM/A9, R8.Pin_1
  N16: Composant1.D10_PWM/A10, R4.Pin_1
  N17: Composant1.D11_PWM, Disp2.pin_11
  N18: Composant1.D12/A11, Composant2.Trig, Composant3.Trig
  N19: Composant1.D13_PWM, R7.Pin_1
  N20: R1.Pin_0, Disp1.pin1, Disp2.pin1
  N21: R2.Pin_0, Disp1.pin2, Disp2.pin2
  N22: R3.Pin_0, Disp1.pin_3, Disp2.pin_3
  N23: R4.Pin_0, Disp1.pin_4, Disp2.pin_4
  N24: R5.Pin_0, Disp1.pin_5, Disp2.pin_5
  N25: R6.Pin_0, Disp1.pin_6, Disp2.pin_6
  N26: R7.Pin_0, Disp1.pin_7, Disp2.pin_7
  N27: R8.Pin_0, Disp1.pin_8, Disp2.pin_8
